# Fritzing sketch Final Fritzing Diagram (saved by Fritzing 0.9.5d)
breadboards: 2

parts:
  Raspberry_Pi_2 = Raspberry Pi 4 [part_number=RPI-4-b]
  LED58 = LED - 5mm [color="Red (633nm)" package="5 mm [THT]"]
  LED59 = LED - 5mm [color="Red (633nm)" package="5 mm [THT]"]
  LED60 = LED - 5mm [color="Red (633nm)" package="5 mm [THT]"]
  LED61 = LED - 5mm [color="Red (633nm)" package="5 mm [THT]"]
  LED62 = LED - 5mm [color="Red (633nm)" package="5 mm [THT]"]
  LED63 = LED - 5mm [color="Red (633nm)" package="5 mm [THT]"]
  LED64 = LED - 5mm [color="Red (633nm)" package="5 mm [THT]"]
  LED65 = LED - 5mm [color="Red (633nm)" package="5 mm [THT]"]
  R58 = Resistor [tolerance=±5% resistance=220 package="0402 [SMD]"]
  R59 = Resistor [tolerance=±5% resistance=220 package="0402 [SMD]"]
  R60 = Resistor [tolerance=±5% resistance=220 package="0402 [SMD]"]
  R61 = Resistor [tolerance=±5% resistance=220 package="0402 [SMD]"]
  R62 = Resistor [tolerance=±5% resistance=220 package="0402 [SMD]"]
  R63 = Resistor [tolerance=±5% resistance=220 package="0402 [SMD]"]
  R64 = Resistor [tolerance=±5% resistance=220 package="0402 [SMD]"]
  R65 = Resistor [tolerance=±5% resistance=220 package="0402 [SMD]"]
  U2 = 74HC595 [package="DIP16 [THT]"]
  IC5 = ULN2803A [package=THT]
  HLK-PM2 = HLK-PM12 [part_number=HLK-PM12]
  U8 = 74HC595 [package="DIP16 [THT]"]
  IC7 = ULN2803A [package=THT]
  LED98 = LED - 5mm [color="Red (633nm)" package="5 mm [THT]"]
  LED99 = LED - 5mm [color="Red (633nm)" package="5 mm [THT]"]
  LED100 = LED - 5mm [color="Red (633nm)" package="5 mm [THT]"]
  LED101 = LED - 5mm [color="Red (633nm)" package="5 mm [THT]"]
  LED102 = LED - 5mm [color="Red (633nm)" package="5 mm [THT]"]
  LED103 = LED - 5mm [color="Red (633nm)" package="5 mm [THT]"]
  LED104 = LED - 5mm [color="Red (633nm)" package="5 mm [THT]"]
  LED105 = LED - 5mm [color="Red (633nm)" package="5 mm [THT]"]
  R98 = Resistor [tolerance=±5% resistance=220 package="0402 [SMD]"]
  R99 = Resistor [tolerance=±5% resistance=220 package="0402 [SMD]"]
  R100 = Resistor [tolerance=±5% resistance=220 package="0402 [SMD]"]
  R101 = Resistor [tolerance=±5% resistance=220 package="0402 [SMD]"]
  R102 = Resistor [tolerance=±5% resistance=220 package="0402 [SMD]"]
  R103 = Resistor [tolerance=±5% resistance=220 package="0402 [SMD]"]
  R104 = Resistor [tolerance=±5% resistance=220 package="0402 [SMD]"]
  R105 = Resistor [tolerance=±5% resistance=220 package="0402 [SMD]"]

nets:
  N1: Raspberry_Pi_2.GPIO10, U2.DS
  N2: Raspberry_Pi_2.GPIO11, U2.SH_CP, U8.SH_CP
  N3: Raspberry_Pi_2.GPIO25, U2.ST_CP, U8.ST_CP
  GND: Raspberry_Pi_2.GND, U2.GND, U2.OE, IC5.0V, HLK-PM2.-Vo, U8.GND, U8.OE, IC7.0V
  VCC: Raspberry_Pi_2.5V, U2.MR, U2.VCC, U8.MR, U8.VCC
  N4: LED58.cathode, IC5.Out_3
  N5: LED59.cathode, IC5.Out_6
  N6: LED60.cathode, IC5.Out_8
  N7: LED61.cathode, IC5.Out_5
  N8: LED62.cathode, IC5.Out_2
  N9: LED63.cathode, IC5.Out_4
  N10: LED64.cathode, IC5.Out_7
  N11: LED65.cathode, IC5.Out_1
  N12: R58.Pin_1, R59.Pin_1, R60.Pin_1, R61.Pin_1, R62.Pin_1, R63.Pin_1, R64.Pin_1, R65.Pin_1, HLK-PM2.+Vo, R98.Pin_1, R99.Pin_1, R100.Pin_1, R101.Pin_1, R102.Pin_1, R103.Pin_1, R104.Pin_1, R105.Pin_1
  N13: U2.Q1, IC5.In_2
  N14: U2.Q2, IC5.In_3
  N15: U2.Q3, IC5.In_4
  N16: U2.Q4, IC5.In_5
  N17: U2.Q5, IC5.In_6
  N18: U2.Q6, IC5.In_7
  N19: U2.Q7, IC5.In_8
  N20: U2.Q7', U8.DS
  N21: U2.Q0, IC5.In_1
  N22: U8.Q1, IC7.In_2
  N23: U8.Q2, IC7.In_3
  N24: U8.Q3, IC7.In_4
  N25: U8.Q4, IC7.In_5
  N26: U8.Q5, IC7.In_6
  N27: U8.Q6, IC7.In_7
  N28: U8.Q7, IC7.In_8
  N29: U8.Q0, IC7.In_1
  N30: IC7.Out_8, LED100.cathode
  N31: IC7.Out_7, LED104.cathode
  N32: IC7.Out_6, LED99.cathode
  N33: IC7.Out_5, LED101.cathode
  N34: IC7.Out_4, LED103.cathode
  N35: IC7.Out_3, LED98.cathode
  N36: IC7.Out_2, LED102.cathode
  N37: IC7.Out_1, LED105.cathode

custom parts:
  Raspberry Pi 4: The RPi4, a faster version of the awesome Raspberry Pi 2 B ARM Board with 40 pin gpio. Ready for special Raspberry Pi B+ and RPi2 Hat (Hardware attached (on) top)
