# Fritzing sketch Fritzing Diagram (saved by Fritzing 0.9.5d)
breadboards: 1

parts:
  Raspberry_Pi_1 = Raspberry Pi 4 [part_number=RPI-4-b]
  U1 = 74HC595 [package="DIP16 [THT]"]
  IC4 = ULN2803A [package=THT]
  LED50 = LED - 5mm [color="Red (633nm)" package="5 mm [THT]"]
  LED51 = LED - 5mm [color="Red (633nm)" package="5 mm [THT]"]
  LED52 = LED - 5mm [color="Red (633nm)" package="5 mm [THT]"]
  LED53 = LED - 5mm [color="Red (633nm)" package="5 mm [THT]"]
  LED54 = LED - 5mm [color="Red (633nm)" package="5 mm [THT]"]
  LED55 = LED - 5mm [color="Red (633nm)" package="5 mm [THT]"]
  LED56 = LED - 5mm [color="Red (633nm)" package="5 mm [THT]"]
  LED57 = LED - 5mm [color="Red (633nm)" package="5 mm [THT]"]
  R50 = Resistor [tolerance=±5% resistance=220 package="0402 [SMD]"]
  R51 = Resistor [tolerance=±5% resistance=220 package="0402 [SMD]"]
  R52 = Resistor [tolerance=±5% resistance=220 package="0402 [SMD]"]
  R53 = Resistor [tolerance=±5% resistance=220 package="0402 [SMD]"]
  R54 = Resistor [tolerance=±5% resistance=220 package="0402 [SMD]"]
  R55 = Resistor [tolerance=±5% resistance=220 package="0402 [SMD]"]
  R56 = Resistor [tolerance=±5% resistance=220 package="0402 [SMD]"]
  R57 = Resistor [tolerance=±5% resistance=220 package="0402 [SMD]"]
  HLK-PM1 = HLK-PM12 [part_number=HLK-PM12]

nets:
  N1: Raspberry_Pi_1.GPIO10, U1.DS
  N2: Raspberry_Pi_1.GPIO11, U1.SH_CP
  GND: Raspberry_Pi_1.GND, U1.GND, U1.OE, IC4.0V, HLK-PM1.-Vo
  N3: Raspberry_Pi_1.GPIO25, U1.ST_CP
  5V: Raspberry_Pi_1.5V, U1.MR, U1.VCC
  N4: U1.Q1, IC4.In_2
  N5: U1.Q2, IC4.In_3
  N6: U1.Q3, IC4.In_4
  N7: U1.Q4, IC4.In_5
  N8: U1.Q5, IC4.In_6
  N9: U1.Q6, IC4.In_7
  N10: U1.Q7, IC4.In_8
  N11: U1.Q0, IC4.In_1
  N12: IC4.Out_8, LED54.cathode
  N13: IC4.Out_7, LED53.cathode
  N14: IC4.Out_6, LED57.cathode
  N15: IC4.Out_5, LED55.cathode
  N16: IC4.Out_4, LED51.cathode
  N17: IC4.Out_3, LED56.cathode
  N18: IC4.Out_2, LED50.cathode
  N19: IC4.Out_1, LED52.cathode
  N20: R50.Pin_1, R51.Pin_1, R52.Pin_1, R53.Pin_1, R54.Pin_1, R55.Pin_1, R56.Pin_1, R57.Pin_1, HLK-PM1.+Vo

custom parts:
  Raspberry Pi 4: The RPi4, a faster version of the awesome Raspberry Pi 2 B ARM Board with 40 pin gpio. Ready for special Raspberry Pi B+ and RPi2 Hat (Hardware attached (on) top)
