# Fritzing sketch OneGroup (saved by Fritzing 0.9.5d)
breadboards: 1

parts:
  U7 = 74HC595 [package="DIP16 [THT]"]
  LED90 = LED - 5mm [color="Red (633nm)" package="5 mm [THT]"]
  IC6 = ULN2803A [package=THT]
  LED91 = LED - 5mm [color="Red (633nm)" package="5 mm [THT]"]
  LED92 = LED - 5mm [color="Red (633nm)" package="5 mm [THT]"]
  LED93 = LED - 5mm [color="Red (633nm)" package="5 mm [THT]"]
  LED94 = LED - 5mm [color="Red (633nm)" package="5 mm [THT]"]
  LED95 = LED - 5mm [color="Red (633nm)" package="5 mm [THT]"]
  LED96 = LED - 5mm [color="Red (633nm)" package="5 mm [THT]"]
  LED97 = LED - 5mm [color="Red (633nm)" package="5 mm [THT]"]
  R90 = Resistor [tolerance=±5% resistance=220 package="0402 [SMD]"]
  R91 = Resistor [tolerance=±5% resistance=220 package="0402 [SMD]"]
  R92 = Resistor [tolerance=±5% resistance=220 package="0402 [SMD]"]
  R93 = Resistor [tolerance=±5% resistance=220 package="0402 [SMD]"]
  R94 = Resistor [tolerance=±5% resistance=220 package="0402 [SMD]"]
  R95 = Resistor [tolerance=±5% resistance=220 package="0402 [SMD]"]
  R96 = Resistor [tolerance=±5% resistance=220 package="0402 [SMD]"]
  R97 = Resistor [tolerance=±5% resistance=220 package="0402 [SMD]"]

nets:
  N1: U7.Q1, IC6.In_2
  N2: U7.Q2, IC6.In_3
  N3: U7.Q3, IC6.In_4
  N4: U7.Q4, IC6.In_5
  N5: U7.Q5, IC6.In_6
  N6: U7.Q6, IC6.In_7
  N7: U7.Q7, IC6.In_8
  N8: U7.GND, U7.OE, IC6.0V
  N9: U7.MR, U7.VCC
  N10: U7.Q0, IC6.In_1
  N11: LED90.cathode, IC6.Out_3
  N12: IC6.Out_8, LED92.cathode
  N13: IC6.Out_7, LED96.cathode
  N14: IC6.Out_6, LED91.cathode
  N15: IC6.Out_5, LED93.cathode
  N16: IC6.Out_4, LED95.cathode
  N17: IC6.Out_2, LED94.cathode
  N18: IC6.Out_1, LED97.cathode
  N19: R90.Pin_1, R91.Pin_1, R92.Pin_1, R93.Pin_1, R94.Pin_1, R95.Pin_1, R96.Pin_1, R97.Pin_1
